# Fritzing sketch FinalProject (saved by Fritzing 0.9.3b)
circuit board: 8.46667cm x 5.64444cm
breadboards: 1

parts:
  Resistor = Resistor [tolerance=±0.05% resistance=10k package=THT]
  Resistor_2 = Resistor [tolerance=±0.05% resistance=330 package=THT]
  Photo_Resistor = Photocell (LDR) [package=THT]
  Part2 = Arduino Uno (Rev3)
  Photo_Resistor_2 = Photocell (LDR) [package=THT]
  Resistor_3 = Resistor [tolerance=±0.05% resistance=330 package=THT]
  Resistor_4 = Resistor [tolerance=±0.05% resistance=10k package=THT]
  Q1 = NPN-Transistor [package="TO92 [THT]"]
  Q2 = NPN-Transistor [package="TO92 [THT]"]
  M1 = DC Motor
  M2 = DC Motor

nets:
  N1: Resistor.Pin_0, Photo_Resistor.pin_1, Part2.A0
  N2: Resistor.Pin_1, Resistor_2.Pin_1, Part2.D9_PWM, Part2.D10_PWM/SS, Part2.GND, Resistor_3.Pin_1, Resistor_4.Pin_1, Q1.E, Q2.E
  N3: Resistor_2.Pin_0, Q2.B
  N4: Photo_Resistor.pin_0, Part2.A1, Part2.5V, Photo_Resistor_2.pin_0, Photo_Resistor_2.pin_1, Resistor_4.Pin_0, M1.pin_2, M2.pin_2
  N5: Resistor_3.Pin_0, Q1.B
  N6: Q1.C, M2.pin_1
  N7: Q2.C, M1.pin_1

// code stored in the sketch: Milestone1.ino
/*  Fall 2018 - CEN 111 Intro to Electrical and Computer Engineering
 *  Final Project: Line-following Robot (Guy-Michel, Andrew)
 *  Milestone #1 : Standard Line Follower
 *  Due : EOD December 10
 */

// Definitions

// light sensor pin definitions
const int leftSensorPin = A0;
const int rightSensorPin = A1;

// motor pin definitions
const int leftMotorPin = 9;
const int rightMotorPin = 10;

// light sensitivity
const int rightLightThreshold = 100;
const int leftLightThreshold = 100;


// Main
void setup(){
  
	// Begin communications
	Serial.begin(9600);
	
	// set Motor pins as output
	pinMode(leftMotorPin, OUTPUT);
	pinMode(rightMotorPin, OUTPUT);
	
	// set Sensor pins as input
	pinMode(leftSensorPin, INPUT);
	pinMode(rightSensorPin, INPUT);
}


void loop(){
  
	// Read sensor values
	int leftLightLevel = analogRead(leftSensorPin);
	int rightLightLevel = analogRead(rightSensorPin);

  
	// If light sensor is greater than threshold
	// then turn motor on, else turn motor off
	
// Left motor
	
	if (leftLightLevel > leftLightThreshold){
	  Serial.println("L = 1");
	  Serial.println(leftLightLevel);
	  digitalWrite(leftMotorPin, HIGH);
	}
	else {
	  Serial.println("L = 0");
	  Serial.println(leftLightLevel);
	  digitalWrite(leftMotorPin, LOW);
	}
  
// Right motor
  
	if (rightLightLevel > rightLightThreshold){
	  Serial.println("R = 1");
	  Serial.println(rightLightLevel);
	  digitalWrite(rightMotorPin, HIGH);
	}
	else {
	  Serial.println("R = 0");
	  Serial.println(rightLightLevel);
	  digitalWrite(rightMotorPin, LOW);
	}
}

// code stored in the sketch: Milestone2.ino
/*  Fall 2018 - CEN 111 Intro to Electrical and Computer Engineering
 *  Final Project: Line-following Robot (Guy-Michel, Andrew)
 *  Milestone #1 : Improved Line Follower
 *  Due : EOD December 10
 */

// Definitions

// light sensor pin definitions
const int leftSensorPin = A0;
const int rightSensorPin = A1;

// motor pin definitions
const int leftMotorPin = 9;
const int rightMotorPin = 10;

// light sensitivity
const int lightThresholdLeft = 210;
const int lightThresholdRight = 550;


// Main
void setup(){
  
  // Begin communications
  Serial.begin(9600);
  
  // set Motor pins as output
  pinMode(leftMotorPin, OUTPUT);
  pinMode(rightMotorPin, OUTPUT);
  
  // set Sensor pins as input
  pinMode(leftSensorPin, INPUT);
  pinMode(rightSensorPin, INPUT);
}


void loop(){
  
  // Read sensor values
  int leftLightLevel = analogRead(leftSensorPin);
  int rightLightLevel = analogRead(rightSensorPin);

  
	if (leftLightLevel > lightThresholdLeft && rightLightLevel < lightThresholdRight){
		// Go Straight
		Serial.println("STRAIGHT");
    Serial.print("L =");
    Serial.println(leftLightLevel);
		Serial.print("R=");
		Serial.println(rightLightLevel);
    digitalWrite(leftMotorPin, HIGH);
    digitalWrite(rightMotorPin, HIGH);
	}
	else if (leftLightLevel > lightThresholdLeft && rightLightLevel > lightThresholdRight){
		// Both Stop
		Serial.println("STOP");
    Serial.print("L =");
    Serial.println(leftLightLevel);
		Serial.print("R=");
		Serial.println(rightLightLevel);
    digitalWrite(leftMotorPin, LOW);
    digitalWrite(rightMotorPin, LOW);
	}
	else if (leftLightLevel < lightThresholdLeft && rightLightLevel > lightThresholdRight){
		// Turn Left
		Serial.println("TURN LEFT");
    Serial.print("L =");
    Serial.println(leftLightLevel);
		Serial.print("R=");
		Serial.println(rightLightLevel);
    digitalWrite(leftMotorPin, LOW);
    digitalWrite(rightMotorPin, HIGH);
	}
	else if (leftLightLevel < lightThresholdLeft && rightLightLevel > lightThresholdRight){
		// Turn Right
		Serial.println("TURN RIGHT");
    Serial.print("L =");
    Serial.println(leftLightLevel);
		Serial.print("R=");
		Serial.println(rightLightLevel);
    digitalWrite(leftMotorPin, HIGH);
    digitalWrite(rightMotorPin, LOW);
	}


}

// code stored in the sketch: Milestone2_button.ino
/*  Fall 2018 - CEN 111 Intro to Electrical and Computer Engineering
 *  Final Project: Line-following Robot (Guy-Michel, Andrew)
 *  Milestone #1 : Improved Line Follower
 *  Due : EOD December 10
 */


// Definitions


// light sensor pin definitions
const int leftSensorPin = A0;
const int rightSensorPin = A1;


// motor pin definitions
const int leftMotorPin = 9;
const int rightMotorPin = 10;


// light sensitivity
const int lightThresholdRight = 210;
const int lightThresholdLeft = 550;
const int lightThresholdTotal = lightThresholdRight + lightThresholdLeft;


// Main
void setup(){
  
    // Begin communications
    Serial.begin(9600);
    
    // set Motor pins as output
    pinMode(leftMotorPin, OUTPUT);
    pinMode(rightMotorPin, OUTPUT);
    
    // set Sensor pins as input
    pinMode(leftSensorPin, INPUT);
    pinMode(rightSensorPin, INPUT);
}




void loop(){
  
    // Read sensor values
    int leftLightLevel = analogRead(leftSensorPin);
    int rightLightLevel = analogRead(rightSensorPin);
    int LightLevelTotal = leftLightLevel + rightLightLevel;
  
    // If light sensor is less than threshold
    // then turn, else run both motors to go forwards


    Serial.println(leftLightLevel);
    Serial.println("^left^");
    Serial.println(rightLightLevel);
    Serial.println("^right^");
    
   
	if (leftLightLevel < lightThresholdLeft){
		// Turn Left
		Serial.println("TURN LEFT");
    Serial.print("L =");
    Serial.println(leftLightLevel);
		Serial.print("R=");
		Serial.println(rightLightLevel);
    digitalWrite(leftMotorPin, LOW);
    digitalWrite(rightMotorPin, HIGH);
		//delay(1000);
		//digitalWrite(rightMotorPin, LOW);
	}
	if (rightLightLevel < lightThresholdRight){
		// Turn Right
		Serial.println("TURN RIGHT");
    Serial.print("L =");
    Serial.println(leftLightLevel);
		Serial.print("R=");
		Serial.println(rightLightLevel);
		digitalWrite(rightMotorPin, LOW);
    digitalWrite(leftMotorPin, HIGH);
		//delay(1000);
    //digitalWrite(leftMotorPin, LOW);
	}


}
